// Logisim project Project.circ as structural Verilog: 29 circuits, main circuit main
module main (
  input  PC_Clear,
  input  DataMem_Clear,
  input  State_Clear,
  input  Register_File_Clear,
  output [19:0] Instruction,
  output [19:0] ALU_Output
);

  wire Clock, DataMem_Read, DataMem_Write, Fetch_Instruction, IMM_Select, PC_Read, Register_Load,
       Register_Read, Register_Write;
  wire [1:0] PC_Write;
  wire [2:0] ALU_Select;
  wire [3:0] DST, REG1, REG2, SRC1, SRC2;
  wire [9:0] ADDR, program_counter_1_output;
  wire [19:0] ALU_Result, DataMem_Result, IMM, multiplexer_1_out, multiplexer_2_out, ram_1_data,
       register_file_1_output_data_1, register_file_1_output_data_2, SR1, SR2;

  Clock clock_1 (.out(Clock));
  Program_Counter program_counter_1 (
    .Input(ADDR), .Select(PC_Write), .Enable(PC_Read), .Clear(PC_Clear), .Clock(Clock),
    .Output(program_counter_1_output));  // open: C_out
  ALU alu_1 (.SR1(SR1), .SR2(SR2), .IMM(IMM), .IMM_Select(IMM_Select), .ALU_Select(ALU_Select), .Output(ALU_Output));
  _20_Bit_Register u_20_bit_register_1 (
    .Input(ALU_Output), .Enable(1'b1), .Clear(1'b0), .Clock(Clock), .Output(ALU_Result));
  ROM #(.addrWidth(10), .dataWidth(20)) rom_1 (.addr(program_counter_1_output), .data(Instruction));  // open: sel
  Control_Unit control_unit_1 (
    .Instruction(Instruction), .Reset_State(State_Clear), .Clock(Clock), .ADDR(ADDR), .SRC2(SRC2), .IMM(IMM),
    .SRC1(SRC1), .DST(DST), .REG2(REG2), .REG1(REG1), .PC_Read(PC_Read),
    .Fetch_Instruction(Fetch_Instruction), .PC_Write(PC_Write), .ALU_Select(ALU_Select),
    .Register_Read(Register_Read), .IMM_Select(IMM_Select), .Register_Write(Register_Write),
    .DataMem_Read(DataMem_Read), .Register_Load(Register_Load), .DataMem_Write(DataMem_Write));
  Multiplexer #(.width(20), .enable("false")) multiplexer_1 (
    .in0(ALU_Result), .in1(DataMem_Result), .out(multiplexer_1_out), .sel(Register_Load));
  RAM #(.addrWidth(10), .dataWidth(20), .bus("separate")) ram_1 (
    .addr(ADDR), .din(SR1), .data(ram_1_data), .str(DataMem_Write), .clk(Clock), .ld(DataMem_Read),
    .clr(DataMem_Clear));  // open: sel
  _20_Bit_Register u_20_bit_register_2 (
    .Input(register_file_1_output_data_1), .Enable(Register_Read), .Clear(Register_File_Clear),
    .Clock(Clock), .Output(SR1));
  Register_File register_file_1 (
    .Input_Data(multiplexer_1_out), .Source_Register_1(SRC1), .Destination_Register(DST),
    .Source_Register_2(SRC2), .Write(Register_Write), .Clear(Register_File_Clear), .Clock(Clock),
    .Output_Data_1(register_file_1_output_data_1), .Output_Data_2(register_file_1_output_data_2));
  _20_Bit_Register u_20_bit_register_3 (
    .Input(register_file_1_output_data_2), .Enable(Register_Read), .Clear(Register_File_Clear),
    .Clock(Clock), .Output(SR2));
  Multiplexer #(.width(20), .enable("false")) multiplexer_2 (
    .in0({20{1'b0}}), .in1(ram_1_data), .out(multiplexer_2_out), .sel(DataMem_Read));
  _20_Bit_Register u_20_bit_register_4 (
    .Input(multiplexer_2_out), .Enable(1'b1), .Clear(1'b0), .Clock(Clock), .Output(DataMem_Result));

  // Notes on the sheet:
  //   Instruction Memory
  //   ALU
  //   contents of rom_1 (hex, n*v repeats v):
  //   82 9a05 13388 1cd0b 2668e 2f805 30bfb 3800a 40082 49a05 53388 5cd0b 6668e 6a000 74000 807fe d640c
  //   Data Memory
  //   Register File
endmodule

module ALU (
  input  [19:0] SR1,
  input  [19:0] SR2,
  input  [19:0] IMM,
  input  IMM_Select,
  input  [2:0] ALU_Select,
  output [19:0] Output
);

  wire [19:0] AND_out, multiplexer_1_out, n20_bit_adder_1_sum, n20_bit_subtractor_1_s, OR_out, XOR_out;

  Multiplexer #(.width(20), .enable("false")) multiplexer_1 (
    .in0(SR2), .in1(IMM), .out(multiplexer_1_out), .sel(IMM_Select));
  _20_Bit_Adder u_20_bit_adder_1 (
    .C_in(1'b0), .Sum(n20_bit_adder_1_sum), .B(SR1), .A(multiplexer_1_out));  // open: C_out
  _20_Bit_Subtractor u_20_bit_subtractor_1 (.A(multiplexer_1_out), .B(SR1), .S(n20_bit_subtractor_1_s));
  assign AND_out = SR1 & multiplexer_1_out;  // AND_Gate AND, 20 bits wide
  assign OR_out = SR1 | multiplexer_1_out;  // OR_Gate OR, 20 bits wide
  assign XOR_out = SR1 ^ multiplexer_1_out;  // XOR_Gate XOR, 20 bits wide
  Multiplexer #(.select(3), .width(20), .enable("false")) multiplexer_2 (
    .in0(n20_bit_adder_1_sum), .in1(n20_bit_subtractor_1_s), .in2(AND_out), .in3(OR_out), .in4(XOR_out),
    .in5({20{1'b0}}), .in6({20{1'b0}}), .in7({20{1'b0}}), .out(Output), .sel(ALU_Select));

  // Notes on the sheet:
  //   ALU
endmodule

// CU
module Control_Unit (
  input  [19:0] Instruction,
  input  Reset_State,
  input  Clock,
  output [9:0] ADDR,
  output [3:0] SRC2,
  output [19:0] IMM,
  output [3:0] SRC1,
  output [3:0] DST,
  output [3:0] REG2,
  output [3:0] REG1,
  output PC_Read,
  output Fetch_Instruction,
  output [1:0] PC_Write,
  output [2:0] ALU_Select,
  output Register_Read,
  output IMM_Select,
  output Register_Write,
  output DataMem_Read,
  output Register_Load,
  output DataMem_Write
);

  wire ADD, ADDI, ALU_State, AND, ANDI, BE, BNE, JUMP, LD, OR, or_1_out, or_2_out, or_3_out, or_4_out, ORI,
       POP, PUSH, Read_State, Reset_State_t, ST, SUB, SUBI, Write_State, XOR, XORI;
  wire [2:0] Counter_output;
  wire [3:0] multiplexer_3_out;

  or or_1 (or_1_out, ADD, SUB, AND, OR, XOR, ST, BE, BNE, ADDI, SUBI, ANDI, ORI, XORI, PUSH);
  and and_1 (Register_Read, or_1_out, Read_State);
  and and_2 (DataMem_Read, Read_State, LD);
  assign IMM = {{13{Instruction[0]}}, {Instruction[0], Instruction[1], Instruction[2], Instruction[3], Instruction[4], Instruction[5], Instruction[6]}};  // Bit_Extender bit_extender_1
  Multiplexer #(.width(4), .enable("false")) multiplexer_1 (
    .in0({Instruction[11], Instruction[12], Instruction[13], Instruction[14]}),
    .in1({Instruction[7], Instruction[8], Instruction[9], Instruction[10]}), .out(SRC1), .sel(ST));
  or or_2 (or_2_out, Reset_State, Reset_State_t);
  Multiplexer #(.width(3), .enable("false")) multiplexer_2 (
    .in0(3'b111), .in1({Instruction[15], Instruction[16], Instruction[17]}), .out(ALU_Select), .sel(ALU_State));
  or or_3 (or_3_out, ADDI, SUBI, ANDI, ORI, XORI);
  Decoder #(.select(3), .enable("false")) decoder_1 (
    .out0(PC_Read), .out1(Fetch_Instruction), .out2(Read_State), .out3(ALU_State), .out4(Write_State),
    .out5(Reset_State_t), .sel(Counter_output));  // open: out6, out7
  _3_Bit_Counter Counter (.Clear(or_2_out), .Clock(Clock), .Output(Counter_output));  // open: C_out
  and and_3 (IMM_Select, ALU_State, or_3_out);
  and and_4 (BE, Instruction[19], ~Instruction[18]);  // AND_Gate
  and and_5 (BNE, Instruction[19], Instruction[18]);
  Decoder #(.select(4), .enable("false")) decoder_2 (
    .out0(ADD), .out1(SUB), .out2(AND), .out3(OR), .out4(XOR), .out5(LD), .out6(ST), .out7(JUMP),
    .out8(ADDI), .out9(SUBI), .out10(ANDI), .out11(ORI), .out12(XORI), .out13(PUSH), .out14(POP),
    .sel(multiplexer_3_out));  // open: out15
  Multiplexer #(.width(4), .enable("false")) multiplexer_3 (
    .in0({Instruction[15], Instruction[16], Instruction[17], Instruction[18]}), .in1(4'b1111),
    .out(multiplexer_3_out), .sel(Instruction[19]));
  or or_4 (or_4_out, ADD, SUB, AND, OR, XOR, ADDI, SUBI, ANDI, ORI, XORI, LD);
  and and_6 (Register_Write, or_4_out, Write_State);
  and and_7 (Register_Load, Write_State, LD);
  and and_8 (DataMem_Write, Write_State, ST);
  and and_9 (PC_Write[1], JUMP, Read_State);
  and and_10 (PC_Write[0], BE, BNE, Read_State);

  assign ADDR = Instruction[9:0];
  assign DST = {Instruction[11], Instruction[12], Instruction[13], Instruction[14]};
  assign REG1 = {Instruction[14], Instruction[15], Instruction[16], Instruction[17]};
  assign REG2 = {Instruction[10], Instruction[11], Instruction[12], Instruction[13]};
  assign SRC2 = Instruction[3:0];

  // Other names for the same wires on the sheet: Opcode1[1:0] = {Instruction[18], Instruction[19]};
  //   Opcode2[2:0] = {Instruction[15], Instruction[16], Instruction[17]}

  // Notes on the sheet:
  //   Control Unit
  //   Signals
  //   State Detector
  //   Instruction Detector
endmodule

module Register_File (
  input  [19:0] Input_Data,
  input  [3:0] Source_Register_1,
  input  [3:0] Destination_Register,
  input  [3:0] Source_Register_2,
  input  Write,
  input  Clear,
  input  Clock,
  output [19:0] Output_Data_1,
  output [19:0] Output_Data_2
);

  wire and_1_out, and_2_out, and_3_out, and_4_out, and_5_out, and_6_out, and_7_out, and_8_out, and_9_out,
       and_10_out, and_11_out, and_12_out, and_13_out, and_14_out, and_15_out, and_16_out, decoder_1_out0,
       decoder_1_out1, decoder_1_out2, decoder_1_out3, decoder_1_out4, decoder_1_out5, decoder_1_out6,
       decoder_1_out7, decoder_1_out8, decoder_1_out9, decoder_1_out10, decoder_1_out11, decoder_1_out12,
       decoder_1_out13, decoder_1_out14, decoder_1_out15;
  wire [19:0] n20_bit_register_1_output, n20_bit_register_2_output, n20_bit_register_3_output,
       n20_bit_register_4_output, n20_bit_register_5_output, n20_bit_register_6_output,
       n20_bit_register_7_output, n20_bit_register_8_output, n20_bit_register_9_output,
       n20_bit_register_10_output, n20_bit_register_11_output, n20_bit_register_12_output,
       n20_bit_register_13_output, n20_bit_register_14_output, n20_bit_register_15_output,
       n20_bit_register_16_output;

  Decoder #(.select(4), .enable("false")) decoder_1 (
    .out0(decoder_1_out0), .out1(decoder_1_out1), .out2(decoder_1_out2), .out3(decoder_1_out3),
    .out4(decoder_1_out4), .out5(decoder_1_out5), .out6(decoder_1_out6), .out7(decoder_1_out7),
    .out8(decoder_1_out8), .out9(decoder_1_out9), .out10(decoder_1_out10), .out11(decoder_1_out11),
    .out12(decoder_1_out12), .out13(decoder_1_out13), .out14(decoder_1_out14), .out15(decoder_1_out15),
    .sel(Destination_Register));
  and and_1 (and_1_out, decoder_1_out0, Write);
  and and_2 (and_2_out, decoder_1_out1, Write);
  and and_3 (and_3_out, decoder_1_out2, Write);
  and and_4 (and_4_out, decoder_1_out3, Write);
  and and_5 (and_5_out, decoder_1_out4, Write);
  and and_6 (and_6_out, decoder_1_out5, Write);
  and and_7 (and_7_out, decoder_1_out6, Write);
  and and_8 (and_8_out, decoder_1_out7, Write);
  and and_9 (and_9_out, decoder_1_out8, Write);
  and and_10 (and_10_out, decoder_1_out9, Write);
  and and_11 (and_11_out, decoder_1_out10, Write);
  and and_12 (and_12_out, decoder_1_out11, Write);
  and and_13 (and_13_out, decoder_1_out12, Write);
  and and_14 (and_14_out, decoder_1_out13, Write);
  and and_15 (and_15_out, decoder_1_out14, Write);
  and and_16 (and_16_out, decoder_1_out15, Write);
  _20_Bit_Register u_20_bit_register_1 (
    .Input(Input_Data), .Enable(and_1_out), .Clear(Clear), .Clock(Clock), .Output(n20_bit_register_1_output));
  _20_Bit_Register u_20_bit_register_2 (
    .Input(Input_Data), .Enable(and_2_out), .Clear(Clear), .Clock(Clock), .Output(n20_bit_register_2_output));
  _20_Bit_Register u_20_bit_register_3 (
    .Input(Input_Data), .Enable(and_3_out), .Clear(Clear), .Clock(Clock), .Output(n20_bit_register_3_output));
  _20_Bit_Register u_20_bit_register_4 (
    .Input(Input_Data), .Enable(and_4_out), .Clear(Clear), .Clock(Clock), .Output(n20_bit_register_4_output));
  _20_Bit_Register u_20_bit_register_5 (
    .Input(Input_Data), .Enable(and_5_out), .Clear(Clear), .Clock(Clock), .Output(n20_bit_register_5_output));
  _20_Bit_Register u_20_bit_register_6 (
    .Input(Input_Data), .Enable(and_6_out), .Clear(Clear), .Clock(Clock), .Output(n20_bit_register_6_output));
  _20_Bit_Register u_20_bit_register_7 (
    .Input(Input_Data), .Enable(and_7_out), .Clear(Clear), .Clock(Clock), .Output(n20_bit_register_7_output));
  _20_Bit_Register u_20_bit_register_8 (
    .Input(Input_Data), .Enable(and_8_out), .Clear(Clear), .Clock(Clock), .Output(n20_bit_register_8_output));
  _20_Bit_Register u_20_bit_register_9 (
    .Input(Input_Data), .Enable(and_9_out), .Clear(Clear), .Clock(Clock), .Output(n20_bit_register_9_output));
  _20_Bit_Register u_20_bit_register_10 (
    .Input(Input_Data), .Enable(and_10_out), .Clear(Clear), .Clock(Clock), .Output(n20_bit_register_10_output));
  _20_Bit_Register u_20_bit_register_11 (
    .Input(Input_Data), .Enable(and_11_out), .Clear(Clear), .Clock(Clock), .Output(n20_bit_register_11_output));
  _20_Bit_Register u_20_bit_register_12 (
    .Input(Input_Data), .Enable(and_12_out), .Clear(Clear), .Clock(Clock), .Output(n20_bit_register_12_output));
  _20_Bit_Register u_20_bit_register_13 (
    .Input(Input_Data), .Enable(and_13_out), .Clear(Clear), .Clock(Clock), .Output(n20_bit_register_13_output));
  _20_Bit_Register u_20_bit_register_14 (
    .Input(Input_Data), .Enable(and_14_out), .Clear(Clear), .Clock(Clock), .Output(n20_bit_register_14_output));
  _20_Bit_Register u_20_bit_register_15 (
    .Input(Input_Data), .Enable(and_15_out), .Clear(Clear), .Clock(Clock), .Output(n20_bit_register_15_output));
  _20_Bit_Register u_20_bit_register_16 (
    .Input(Input_Data), .Enable(and_16_out), .Clear(Clear), .Clock(Clock), .Output(n20_bit_register_16_output));
  Multiplexer #(.select(4), .width(20), .enable("false")) multiplexer_1 (
    .in0(n20_bit_register_1_output), .in1(n20_bit_register_2_output), .in2(n20_bit_register_3_output),
    .in3(n20_bit_register_4_output), .in4(n20_bit_register_5_output), .in5(n20_bit_register_6_output),
    .in6(n20_bit_register_7_output), .in7(n20_bit_register_8_output), .in8(n20_bit_register_9_output),
    .in9(n20_bit_register_10_output), .in10(n20_bit_register_11_output), .in11(n20_bit_register_12_output),
    .in12(n20_bit_register_13_output), .in13(n20_bit_register_14_output), .in14(n20_bit_register_15_output),
    .in15(n20_bit_register_16_output), .out(Output_Data_1), .sel(Source_Register_1));
  Multiplexer #(.select(4), .width(20), .enable("false")) multiplexer_2 (
    .in0(n20_bit_register_1_output), .in1(n20_bit_register_2_output), .in2(n20_bit_register_3_output),
    .in3(n20_bit_register_4_output), .in4(n20_bit_register_5_output), .in5(n20_bit_register_6_output),
    .in6(n20_bit_register_7_output), .in7(n20_bit_register_8_output), .in8(n20_bit_register_9_output),
    .in9(n20_bit_register_10_output), .in10(n20_bit_register_11_output), .in11(n20_bit_register_12_output),
    .in12(n20_bit_register_13_output), .in13(n20_bit_register_14_output), .in14(n20_bit_register_15_output),
    .in15(n20_bit_register_16_output), .out(Output_Data_2), .sel(Source_Register_2));

  // Notes on the sheet:
  //   Register File
endmodule

// PC
module Program_Counter (
  input  [9:0] Input,
  input  [1:0] Select,
  input  Enable,
  input  Clear,
  input  Clock,
  output C_out,
  output [9:0] Output
);

  wire [9:0] multiplexer_1_out, multiplexer_2_out, n10_bit_adder_1_sum;

  Multiplexer #(.width(10), .enable("false")) multiplexer_1 (
    .in0(n10_bit_adder_1_sum), .in1(Input), .out(multiplexer_1_out), .sel(Select[0]));
  _10_Bit_Register u_10_bit_register_1 (
    .Input(multiplexer_1_out), .Enable(Enable), .Clear(Clear), .Clock(Clock), .Output(Output));
  Multiplexer #(.width(10), .enable("false")) multiplexer_2 (
    .in0(10'h1), .in1(Input), .out(multiplexer_2_out), .sel(Select[1]));
  _10_Bit_Adder u_10_bit_adder_1 (
    .C_in(1'b0), .B(Output), .A(multiplexer_2_out), .Sum(n10_bit_adder_1_sum), .C_out(C_out));

  // Notes on the sheet:
  //   Program Counter
endmodule

module _3_Bit_Counter (
  input  Clear,
  input  Clock,
  output C_out,
  output [2:0] Output
);

  wire [2:0] n3_bit_adder_1_sum;

  _3_Bit_Register u_3_bit_register_1 (
    .Input(n3_bit_adder_1_sum), .Enable(1'b1), .Clear(Clear), .Clock(Clock), .Output(Output));
  _3_Bit_Adder u_3_bit_adder_1 (.C_in(1'b0), .B(Output), .A(3'b001), .Sum(n3_bit_adder_1_sum), .C_out(C_out));

  // Notes on the sheet:
  //   3-Bit Counter
endmodule

module D_Latch (
  input  Data,
  input  Clock,
  output Output
);

  wire and_1_out, and_2_out, half_adder_1_c_out, half_adder_1_s, multiplexer_1_out, nand_1_out, nor_1_out,
       not_1_out, register_1_q;

  not not_1 (not_1_out, Data);
  Half_Adder half_adder_1 (.A(Clock), .B(register_1_q), .S(half_adder_1_s), .C_out(half_adder_1_c_out));
  and and_1 (and_1_out, Data, Clock);
  and and_2 (and_2_out, Clock, not_1_out);
  nand nand_1 (nand_1_out, half_adder_1_s, half_adder_1_c_out);
  Register #(.width(1)) register_1 (.D(nand_1_out), .Q(register_1_q), .clk(Clock));  // open: en, clr
  nor nor_1 (nor_1_out, and_1_out, Output);
  nor nor_2 (Output, multiplexer_1_out, and_2_out);
  Multiplexer #(.enable("false")) multiplexer_1 (
    .in0(1'b1), .in1(nor_1_out), .out(multiplexer_1_out), .sel(register_1_q));

  // Notes on the sheet:
  //   D-Latch
  //   Initialization
endmodule

module D_Flip_Flop (
  input  Data,
  input  Clock,
  output out_3
);

  wire d_latch_1_output, not_1_out;

  not not_1 (not_1_out, Clock);
  D_Latch d_latch_1 (.Data(Data), .Clock(not_1_out), .Output(d_latch_1_output));
  D_Latch d_latch_2 (.Data(d_latch_1_output), .Clock(Clock), .Output(out_3));

  // Notes on the sheet:
  //   D-Flip Flop
endmodule

// Register
module _3_Bit_Register (
  input  [2:0] Input,
  input  Enable,
  input  Clear,
  input  Clock,
  output [2:0] Output
);

  wire multiplexer_1_out, multiplexer_2_out, multiplexer_3_out;
  wire [0:0] not_1_out;

  not not_1 (not_1_out[0], Enable);
  Multiplexer #(.select(2), .enable("false")) multiplexer_1 (
    .in0(Input[2]), .in1(Output[2]), .in2(1'b0), .in3(1'b0), .out(multiplexer_1_out),
    .sel({Clear, not_1_out[0]}));
  D_Flip_Flop d_flip_flop_1 (.Data(multiplexer_1_out), .Clock(Clock), .out_3(Output[2]));
  Multiplexer #(.select(2), .enable("false")) multiplexer_2 (
    .in0(Input[1]), .in1(Output[1]), .in2(1'b0), .in3(1'b0), .out(multiplexer_2_out),
    .sel({Clear, not_1_out[0]}));
  D_Flip_Flop d_flip_flop_2 (.Data(multiplexer_2_out), .Clock(Clock), .out_3(Output[1]));
  Multiplexer #(.select(2), .enable("false")) multiplexer_3 (
    .in0(Input[0]), .in1(Output[0]), .in2(1'b0), .in3(1'b0), .out(multiplexer_3_out),
    .sel({Clear, not_1_out[0]}));
  D_Flip_Flop d_flip_flop_3 (.Data(multiplexer_3_out), .Clock(Clock), .out_3(Output[0]));

  // Notes on the sheet:
  //   3-Bit Register
endmodule

// Register
module _10_Bit_Register (
  input  [9:0] Input,
  input  Enable,
  input  Clear,
  input  Clock,
  output [9:0] Output
);

  wire multiplexer_1_out, multiplexer_2_out, multiplexer_3_out, multiplexer_4_out, multiplexer_5_out,
       multiplexer_6_out, multiplexer_7_out, multiplexer_8_out, multiplexer_9_out, multiplexer_10_out;
  wire [0:0] not_1_out;

  not not_1 (not_1_out[0], Enable);
  Multiplexer #(.select(2), .enable("false")) multiplexer_1 (
    .in0(Input[9]), .in1(Output[9]), .in2(1'b0), .in3(1'b0), .out(multiplexer_1_out),
    .sel({Clear, not_1_out[0]}));
  D_Flip_Flop d_flip_flop_1 (.Data(multiplexer_1_out), .Clock(Clock), .out_3(Output[9]));
  Multiplexer #(.select(2), .enable("false")) multiplexer_2 (
    .in0(Input[8]), .in1(Output[8]), .in2(1'b0), .in3(1'b0), .out(multiplexer_2_out),
    .sel({Clear, not_1_out[0]}));
  D_Flip_Flop d_flip_flop_2 (.Data(multiplexer_2_out), .Clock(Clock), .out_3(Output[8]));
  Multiplexer #(.select(2), .enable("false")) multiplexer_3 (
    .in0(Input[7]), .in1(Output[7]), .in2(1'b0), .in3(1'b0), .out(multiplexer_3_out),
    .sel({Clear, not_1_out[0]}));
  D_Flip_Flop d_flip_flop_3 (.Data(multiplexer_3_out), .Clock(Clock), .out_3(Output[7]));
  Multiplexer #(.select(2), .enable("false")) multiplexer_4 (
    .in0(Input[6]), .in1(Output[6]), .in2(1'b0), .in3(1'b0), .out(multiplexer_4_out),
    .sel({Clear, not_1_out[0]}));
  D_Flip_Flop d_flip_flop_4 (.Data(multiplexer_4_out), .Clock(Clock), .out_3(Output[6]));
  Multiplexer #(.select(2), .enable("false")) multiplexer_5 (
    .in0(Input[5]), .in1(Output[5]), .in2(1'b0), .in3(1'b0), .out(multiplexer_5_out),
    .sel({Clear, not_1_out[0]}));
  D_Flip_Flop d_flip_flop_5 (.Data(multiplexer_5_out), .Clock(Clock), .out_3(Output[5]));
  Multiplexer #(.select(2), .enable("false")) multiplexer_6 (
    .in0(Input[4]), .in1(Output[4]), .in2(1'b0), .in3(1'b0), .out(multiplexer_6_out),
    .sel({Clear, not_1_out[0]}));
  D_Flip_Flop d_flip_flop_6 (.Data(multiplexer_6_out), .Clock(Clock), .out_3(Output[4]));
  Multiplexer #(.select(2), .enable("false")) multiplexer_7 (
    .in0(Input[3]), .in1(Output[3]), .in2(1'b0), .in3(1'b0), .out(multiplexer_7_out),
    .sel({Clear, not_1_out[0]}));
  D_Flip_Flop d_flip_flop_7 (.Data(multiplexer_7_out), .Clock(Clock), .out_3(Output[3]));
  Multiplexer #(.select(2), .enable("false")) multiplexer_8 (
    .in0(Input[2]), .in1(Output[2]), .in2(1'b0), .in3(1'b0), .out(multiplexer_8_out),
    .sel({Clear, not_1_out[0]}));
  D_Flip_Flop d_flip_flop_8 (.Data(multiplexer_8_out), .Clock(Clock), .out_3(Output[2]));
  Multiplexer #(.select(2), .enable("false")) multiplexer_9 (
    .in0(Input[1]), .in1(Output[1]), .in2(1'b0), .in3(1'b0), .out(multiplexer_9_out),
    .sel({Clear, not_1_out[0]}));
  D_Flip_Flop d_flip_flop_9 (.Data(multiplexer_9_out), .Clock(Clock), .out_3(Output[1]));
  Multiplexer #(.select(2), .enable("false")) multiplexer_10 (
    .in0(Input[0]), .in1(Output[0]), .in2(1'b0), .in3(1'b0), .out(multiplexer_10_out),
    .sel({Clear, not_1_out[0]}));
  D_Flip_Flop d_flip_flop_10 (.Data(multiplexer_10_out), .Clock(Clock), .out_3(Output[0]));

  // Notes on the sheet:
  //   10-Bit Register
endmodule

// Register
module _20_Bit_Register (
  input  [19:0] Input,
  input  Enable,
  input  Clear,
  input  Clock,
  output [19:0] Output
);

  wire multiplexer_1_out, multiplexer_2_out, multiplexer_3_out, multiplexer_4_out, multiplexer_5_out,
       multiplexer_6_out, multiplexer_7_out, multiplexer_8_out, multiplexer_9_out, multiplexer_10_out,
       multiplexer_11_out, multiplexer_12_out, multiplexer_13_out, multiplexer_14_out, multiplexer_15_out,
       multiplexer_16_out, multiplexer_17_out, multiplexer_18_out, multiplexer_19_out, multiplexer_20_out;
  wire [0:0] not_1_out;

  not not_1 (not_1_out[0], Enable);
  Multiplexer #(.select(2), .enable("false")) multiplexer_1 (
    .in0(Input[19]), .in1(Output[19]), .in2(1'b0), .in3(1'b0), .out(multiplexer_1_out),
    .sel({Clear, not_1_out[0]}));
  D_Flip_Flop d_flip_flop_1 (.Data(multiplexer_1_out), .Clock(Clock), .out_3(Output[19]));
  Multiplexer #(.select(2), .enable("false")) multiplexer_2 (
    .in0(Input[18]), .in1(Output[18]), .in2(1'b0), .in3(1'b0), .out(multiplexer_2_out),
    .sel({Clear, not_1_out[0]}));
  D_Flip_Flop d_flip_flop_2 (.Data(multiplexer_2_out), .Clock(Clock), .out_3(Output[18]));
  Multiplexer #(.select(2), .enable("false")) multiplexer_3 (
    .in0(Input[17]), .in1(Output[17]), .in2(1'b0), .in3(1'b0), .out(multiplexer_3_out),
    .sel({Clear, not_1_out[0]}));
  D_Flip_Flop d_flip_flop_3 (.Data(multiplexer_3_out), .Clock(Clock), .out_3(Output[17]));
  Multiplexer #(.select(2), .enable("false")) multiplexer_4 (
    .in0(Input[16]), .in1(Output[16]), .in2(1'b0), .in3(1'b0), .out(multiplexer_4_out),
    .sel({Clear, not_1_out[0]}));
  D_Flip_Flop d_flip_flop_4 (.Data(multiplexer_4_out), .Clock(Clock), .out_3(Output[16]));
  Multiplexer #(.select(2), .enable("false")) multiplexer_5 (
    .in0(Input[15]), .in1(Output[15]), .in2(1'b0), .in3(1'b0), .out(multiplexer_5_out),
    .sel({Clear, not_1_out[0]}));
  D_Flip_Flop d_flip_flop_5 (.Data(multiplexer_5_out), .Clock(Clock), .out_3(Output[15]));
  Multiplexer #(.select(2), .enable("false")) multiplexer_6 (
    .in0(Input[14]), .in1(Output[14]), .in2(1'b0), .in3(1'b0), .out(multiplexer_6_out),
    .sel({Clear, not_1_out[0]}));
  D_Flip_Flop d_flip_flop_6 (.Data(multiplexer_6_out), .Clock(Clock), .out_3(Output[14]));
  Multiplexer #(.select(2), .enable("false")) multiplexer_7 (
    .in0(Input[13]), .in1(Output[13]), .in2(1'b0), .in3(1'b0), .out(multiplexer_7_out),
    .sel({Clear, not_1_out[0]}));
  D_Flip_Flop d_flip_flop_7 (.Data(multiplexer_7_out), .Clock(Clock), .out_3(Output[13]));
  Multiplexer #(.select(2), .enable("false")) multiplexer_8 (
    .in0(Input[12]), .in1(Output[12]), .in2(1'b0), .in3(1'b0), .out(multiplexer_8_out),
    .sel({Clear, not_1_out[0]}));
  D_Flip_Flop d_flip_flop_8 (.Data(multiplexer_8_out), .Clock(Clock), .out_3(Output[12]));
  Multiplexer #(.select(2), .enable("false")) multiplexer_9 (
    .in0(Input[11]), .in1(Output[11]), .in2(1'b0), .in3(1'b0), .out(multiplexer_9_out),
    .sel({Clear, not_1_out[0]}));
  D_Flip_Flop d_flip_flop_9 (.Data(multiplexer_9_out), .Clock(Clock), .out_3(Output[11]));
  Multiplexer #(.select(2), .enable("false")) multiplexer_10 (
    .in0(Input[10]), .in1(Output[10]), .in2(1'b0), .in3(1'b0), .out(multiplexer_10_out),
    .sel({Clear, not_1_out[0]}));
  D_Flip_Flop d_flip_flop_10 (.Data(multiplexer_10_out), .Clock(Clock), .out_3(Output[10]));
  Multiplexer #(.select(2), .enable("false")) multiplexer_11 (
    .in0(Input[9]), .in1(Output[9]), .in2(1'b0), .in3(1'b0), .out(multiplexer_11_out),
    .sel({Clear, not_1_out[0]}));
  D_Flip_Flop d_flip_flop_11 (.Data(multiplexer_11_out), .Clock(Clock), .out_3(Output[9]));
  Multiplexer #(.select(2), .enable("false")) multiplexer_12 (
    .in0(Input[8]), .in1(Output[8]), .in2(1'b0), .in3(1'b0), .out(multiplexer_12_out),
    .sel({Clear, not_1_out[0]}));
  D_Flip_Flop d_flip_flop_12 (.Data(multiplexer_12_out), .Clock(Clock), .out_3(Output[8]));
  Multiplexer #(.select(2), .enable("false")) multiplexer_13 (
    .in0(Input[7]), .in1(Output[7]), .in2(1'b0), .in3(1'b0), .out(multiplexer_13_out),
    .sel({Clear, not_1_out[0]}));
  D_Flip_Flop d_flip_flop_13 (.Data(multiplexer_13_out), .Clock(Clock), .out_3(Output[7]));
  Multiplexer #(.select(2), .enable("false")) multiplexer_14 (
    .in0(Input[6]), .in1(Output[6]), .in2(1'b0), .in3(1'b0), .out(multiplexer_14_out),
    .sel({Clear, not_1_out[0]}));
  D_Flip_Flop d_flip_flop_14 (.Data(multiplexer_14_out), .Clock(Clock), .out_3(Output[6]));
  Multiplexer #(.select(2), .enable("false")) multiplexer_15 (
    .in0(Input[5]), .in1(Output[5]), .in2(1'b0), .in3(1'b0), .out(multiplexer_15_out),
    .sel({Clear, not_1_out[0]}));
  D_Flip_Flop d_flip_flop_15 (.Data(multiplexer_15_out), .Clock(Clock), .out_3(Output[5]));
  Multiplexer #(.select(2), .enable("false")) multiplexer_16 (
    .in0(Input[4]), .in1(Output[4]), .in2(1'b0), .in3(1'b0), .out(multiplexer_16_out),
    .sel({Clear, not_1_out[0]}));
  D_Flip_Flop d_flip_flop_16 (.Data(multiplexer_16_out), .Clock(Clock), .out_3(Output[4]));
  Multiplexer #(.select(2), .enable("false")) multiplexer_17 (
    .in0(Input[3]), .in1(Output[3]), .in2(1'b0), .in3(1'b0), .out(multiplexer_17_out),
    .sel({Clear, not_1_out[0]}));
  D_Flip_Flop d_flip_flop_17 (.Data(multiplexer_17_out), .Clock(Clock), .out_3(Output[3]));
  Multiplexer #(.select(2), .enable("false")) multiplexer_18 (
    .in0(Input[2]), .in1(Output[2]), .in2(1'b0), .in3(1'b0), .out(multiplexer_18_out),
    .sel({Clear, not_1_out[0]}));
  D_Flip_Flop d_flip_flop_18 (.Data(multiplexer_18_out), .Clock(Clock), .out_3(Output[2]));
  Multiplexer #(.select(2), .enable("false")) multiplexer_19 (
    .in0(Input[1]), .in1(Output[1]), .in2(1'b0), .in3(1'b0), .out(multiplexer_19_out),
    .sel({Clear, not_1_out[0]}));
  D_Flip_Flop d_flip_flop_19 (.Data(multiplexer_19_out), .Clock(Clock), .out_3(Output[1]));
  Multiplexer #(.select(2), .enable("false")) multiplexer_20 (
    .in0(Input[0]), .in1(Output[0]), .in2(1'b0), .in3(1'b0), .out(multiplexer_20_out),
    .sel({Clear, not_1_out[0]}));
  D_Flip_Flop d_flip_flop_20 (.Data(multiplexer_20_out), .Clock(Clock), .out_3(Output[0]));

  // Notes on the sheet:
  //   20-Bit Register
endmodule

module Half_Adder (
  input  A,
  input  B,
  output S,
  output C_out
);

  xor xor_1 (S, A, B);
  and and_1 (C_out, A, B);

  // Notes on the sheet:
  //   Half Adder
endmodule

module Full_Adder (
  input  A,
  input  B,
  input  C_in,
  output S,
  output C_out
);

  wire and_1_out, and_2_out, and_3_out;

  xor xor_1 (S, A, B, C_in);
  and and_1 (and_1_out, A, B);
  and and_2 (and_2_out, A, C_in);
  and and_3 (and_3_out, B, C_in);
  or or_1 (C_out, and_1_out, and_2_out, and_3_out);

  // Notes on the sheet:
  //   Full Adder
endmodule

module _2_Bit_Adder (
  input  [1:0] B,
  input  [1:0] A,
  input  C_in,
  output [1:0] Sum,
  output C_out
);

  wire full_adder_1_c_out;

  Full_Adder full_adder_1 (.A(A[0]), .B(B[0]), .C_in(C_in), .S(Sum[0]), .C_out(full_adder_1_c_out));
  Full_Adder full_adder_2 (.A(A[1]), .B(B[1]), .C_in(full_adder_1_c_out), .S(Sum[1]), .C_out(C_out));

  // Notes on the sheet:
  //   2-Bit Adder
endmodule

module _3_Bit_Adder (
  input  [2:0] B,
  input  [2:0] A,
  input  C_in,
  output [2:0] Sum,
  output C_out
);

  wire n2_bit_adder_1_c_out;

  _2_Bit_Adder u_2_bit_adder_1 (.C_in(C_in), .B(B[1:0]), .A(A[1:0]), .Sum(Sum[1:0]), .C_out(n2_bit_adder_1_c_out));
  Full_Adder full_adder_1 (.A(A[2]), .B(B[2]), .C_in(n2_bit_adder_1_c_out), .S(Sum[2]), .C_out(C_out));

  // Notes on the sheet:
  //   3-Bit Adder
endmodule

module _4_Bit_Adder (
  input  [3:0] B,
  input  [3:0] A,
  input  C_in,
  output [3:0] Sum,
  output C_out
);

  wire n2_bit_adder_1_c_out;

  _2_Bit_Adder u_2_bit_adder_1 (.C_in(C_in), .B(B[1:0]), .A(A[1:0]), .Sum(Sum[1:0]), .C_out(n2_bit_adder_1_c_out));
  _2_Bit_Adder u_2_bit_adder_2 (.C_in(n2_bit_adder_1_c_out), .B(B[3:2]), .A(A[3:2]), .Sum(Sum[3:2]), .C_out(C_out));

  // Notes on the sheet:
  //   4-Bit Adder
endmodule

module _8_Bit_Adder (
  input  [7:0] B,
  input  [7:0] A,
  input  C_in,
  output [7:0] Sum,
  output C_out
);

  wire n4_bit_adder_1_c_out;

  _4_Bit_Adder u_4_bit_adder_1 (.C_in(C_in), .B(B[3:0]), .A(A[3:0]), .Sum(Sum[3:0]), .C_out(n4_bit_adder_1_c_out));
  _4_Bit_Adder u_4_bit_adder_2 (.C_in(n4_bit_adder_1_c_out), .B(B[7:4]), .A(A[7:4]), .Sum(Sum[7:4]), .C_out(C_out));

  // Notes on the sheet:
  //   8-Bit Adder
endmodule

module _10_Bit_Adder (
  input  [9:0] B,
  input  [9:0] A,
  input  C_in,
  output [9:0] Sum,
  output C_out
);

  wire n8_bit_adder_1_c_out;

  _8_Bit_Adder u_8_bit_adder_1 (.C_in(C_in), .B(B[7:0]), .A(A[7:0]), .Sum(Sum[7:0]), .C_out(n8_bit_adder_1_c_out));
  _2_Bit_Adder u_2_bit_adder_1 (.C_in(n8_bit_adder_1_c_out), .B(B[9:8]), .A(A[9:8]), .Sum(Sum[9:8]), .C_out(C_out));

  // Notes on the sheet:
  //   10-Bit Adder
endmodule

module _16_Bit_Adder (
  input  [15:0] B,
  input  [15:0] A,
  input  C_in,
  output [15:0] Sum,
  output C_out
);

  wire n8_bit_adder_1_c_out;

  _8_Bit_Adder u_8_bit_adder_1 (.C_in(C_in), .B(B[7:0]), .A(A[7:0]), .Sum(Sum[7:0]), .C_out(n8_bit_adder_1_c_out));
  _8_Bit_Adder u_8_bit_adder_2 (.C_in(n8_bit_adder_1_c_out), .B(B[15:8]), .A(A[15:8]), .Sum(Sum[15:8]), .C_out(C_out));

  // Notes on the sheet:
  //   16-Bit Adder
endmodule

// ADD
module _20_Bit_Adder (
  input  [19:0] B,
  input  [19:0] A,
  input  C_in,
  output [19:0] Sum,
  output C_out
);

  wire n16_bit_adder_1_c_out;

  _16_Bit_Adder u_16_bit_adder_1 (
    .C_in(C_in), .B(B[15:0]), .A(A[15:0]), .Sum(Sum[15:0]), .C_out(n16_bit_adder_1_c_out));
  _4_Bit_Adder u_4_bit_adder_1 (
    .C_in(n16_bit_adder_1_c_out), .B(B[19:16]), .A(A[19:16]), .Sum(Sum[19:16]), .C_out(C_out));

  // Notes on the sheet:
  //   20-Bit Adder
endmodule

module _20_Bit_Adder_Subtractor (
  input  [19:0] A,
  input  [19:0] B,
  input  Sub,
  output [19:0] S
);

  wire [19:0] multiplexer_1_out, not_1_out;

  assign not_1_out = ~B;  // NOT_Gate not_1, 20 bits wide
  Multiplexer #(.width(20), .enable("false")) multiplexer_1 (
    .in0(B), .in1(not_1_out), .out(multiplexer_1_out), .sel(Sub));
  _20_Bit_Adder u_20_bit_adder_1 (.C_in(Sub), .Sum(S), .B(multiplexer_1_out), .A(A));  // open: C_out

  // Notes on the sheet:
  //   20-Bit Adder/Subtractor
endmodule

// SUB
module _20_Bit_Subtractor (
  input  [19:0] A,
  input  [19:0] B,
  output [19:0] S
);

  wire [19:0] not_1_out;

  assign not_1_out = ~B;  // NOT_Gate not_1, 20 bits wide
  _20_Bit_Adder u_20_bit_adder_1 (.C_in(1'b1), .Sum(S), .B(not_1_out), .A(A));  // open: C_out

  // Notes on the sheet:
  //   20-Bit Subtractor
endmodule

module Half_Comparator (
  input  A,
  input  B,
  output eq,
  output ls,
  output gt
);

  wire not_1_out, not_2_out;

  not not_1 (not_1_out, A);
  not not_2 (not_2_out, B);
  xnor xnor_1 (eq, A, B);
  and and_1 (ls, not_1_out, B);
  and and_2 (gt, A, not_2_out);

  // Notes on the sheet:
  //   Half Comparator
endmodule

module Full_Comparator (
  input  A,
  input  B,
  input  eq_in,
  input  lt_in,
  input  gt_in,
  output lt,
  output gt,
  output eq
);

  wire and_1_out, and_2_out, not_1_out, not_2_out, xnor_1_out;

  not not_1 (not_1_out, A);
  not not_2 (not_2_out, B);
  and and_1 (and_1_out, not_1_out, B, eq_in);
  and and_2 (and_2_out, eq_in, A, not_2_out);
  xnor xnor_1 (xnor_1_out, A, B);
  or or_1 (lt, and_1_out, lt_in);
  or or_2 (gt, and_2_out, gt_in);
  and and_3 (eq, xnor_1_out, eq_in);

  // Notes on the sheet:
  //   Full Comparator
endmodule

module _2_Bit_Comparator (
  input  [1:0] A,
  input  [1:0] B,
  input  eq_in,
  input  lt_in,
  input  gt_in,
  output eq,
  output lt,
  output gt
);

  wire full_comparator_1_eq, full_comparator_1_gt, full_comparator_1_lt;

  Full_Comparator full_comparator_1 (
    .A(A[1]), .B(B[1]), .eq_in(eq_in), .lt(full_comparator_1_lt), .lt_in(lt_in), .gt_in(gt_in),
    .gt(full_comparator_1_gt), .eq(full_comparator_1_eq));
  Full_Comparator full_comparator_2 (
    .A(A[0]), .B(B[0]), .eq_in(full_comparator_1_eq), .lt(lt), .lt_in(full_comparator_1_lt),
    .gt_in(full_comparator_1_gt), .gt(gt), .eq(eq));

  // Notes on the sheet:
  //   2-Bit Comparator
endmodule

module _4_Bit_Comparator (
  input  [3:0] A,
  input  [3:0] B,
  input  eq_in,
  input  lt_in,
  input  gt_in,
  output eq,
  output lt,
  output gt
);

  wire n2_bit_comparator_2_eq, n2_bit_comparator_2_gt, n2_bit_comparator_2_lt;

  _2_Bit_Comparator u_2_bit_comparator_1 (
    .A(A[1:0]), .B(B[1:0]), .eq_in(n2_bit_comparator_2_eq), .lt_in(n2_bit_comparator_2_lt),
    .gt_in(n2_bit_comparator_2_gt), .lt(lt), .gt(gt), .eq(eq));
  _2_Bit_Comparator u_2_bit_comparator_2 (
    .A(A[3:2]), .B(B[3:2]), .eq_in(eq_in), .lt_in(lt_in), .gt_in(gt_in), .lt(n2_bit_comparator_2_lt),
    .gt(n2_bit_comparator_2_gt), .eq(n2_bit_comparator_2_eq));

  // Notes on the sheet:
  //   4-Bit Comparator
endmodule

module _8_Bit_Comparator (
  input  [7:0] A,
  input  [7:0] B,
  input  eq_in,
  input  lt_in,
  input  gt_in,
  output eq,
  output lt,
  output gt
);

  wire n4_bit_comparator_1_eq, n4_bit_comparator_1_gt, n4_bit_comparator_1_lt;

  _4_Bit_Comparator u_4_bit_comparator_1 (
    .A(A[7:4]), .B(B[7:4]), .eq_in(eq_in), .lt_in(lt_in), .gt_in(gt_in), .eq(n4_bit_comparator_1_eq),
    .lt(n4_bit_comparator_1_lt), .gt(n4_bit_comparator_1_gt));
  _4_Bit_Comparator u_4_bit_comparator_2 (
    .A(A[3:0]), .B(B[3:0]), .eq_in(n4_bit_comparator_1_eq), .lt_in(n4_bit_comparator_1_lt),
    .gt_in(n4_bit_comparator_1_gt), .eq(eq), .lt(lt), .gt(gt));

  // Notes on the sheet:
  //   8-Bit Comparator
endmodule

module _16_Bit_Comparator (
  input  [15:0] A,
  input  [15:0] B,
  input  eq_in,
  input  lt_in,
  input  gt_in,
  output eq,
  output lt,
  output gt
);

  wire n8_bit_comparator_2_eq, n8_bit_comparator_2_gt, n8_bit_comparator_2_lt;

  _8_Bit_Comparator u_8_bit_comparator_1 (
    .A(A[7:0]), .B(B[7:0]), .eq_in(n8_bit_comparator_2_eq), .lt_in(n8_bit_comparator_2_lt),
    .gt_in(n8_bit_comparator_2_gt), .eq(eq), .lt(lt), .gt(gt));
  _8_Bit_Comparator u_8_bit_comparator_2 (
    .A(A[15:8]), .B(B[15:8]), .eq_in(eq_in), .lt_in(lt_in), .gt_in(gt_in), .eq(n8_bit_comparator_2_eq),
    .lt(n8_bit_comparator_2_lt), .gt(n8_bit_comparator_2_gt));

  // Notes on the sheet:
  //   16-Bit Comparator
endmodule

module _20_Bit_Comparator (
  input  [19:0] A,
  input  [19:0] B,
  input  eq_in,
  input  lt_in,
  input  gt_in,
  output eq,
  output lt,
  output gt
);

  wire n16_bit_comparator_1_eq, n16_bit_comparator_1_gt, n16_bit_comparator_1_lt;

  _16_Bit_Comparator u_16_bit_comparator_1 (
    .A(A[19:4]), .B(B[19:4]), .eq_in(eq_in), .lt_in(lt_in), .gt_in(gt_in), .eq(n16_bit_comparator_1_eq),
    .lt(n16_bit_comparator_1_lt), .gt(n16_bit_comparator_1_gt));
  _4_Bit_Comparator u_4_bit_comparator_1 (
    .A(A[3:0]), .B(B[3:0]), .eq_in(n16_bit_comparator_1_eq), .lt_in(n16_bit_comparator_1_lt),
    .gt_in(n16_bit_comparator_1_gt), .eq(eq), .lt(lt), .gt(gt));

  // Notes on the sheet:
  //   20-Bit Comparator
endmodule
